# Fritzing sketch Group3_Clean (saved by Fritzing 0.9.9b)
circuit board: 11.0242cm x 10.5199cm
breadboards: 1

parts:
  R1 = Photocell (LDR) [package=THT]
  U4 = NodeMCU V1.0
  OLED2 = OLED 128x64 I2C Monochrome Display GND-VDD
  Part2 = Real Time Clock Module - DS1307 RTC Breakout Board
  Part3 = Adafruit SPI Flash SD Card [part_number="Adafruit #4899"]
  DHT1 = DHT11 Humitidy and Temperature Sensor
  GY2 = MPU-6050 Board GY-521 [form="♀ (female)" package=THT]
  Part4 = Adafruit BME680 [part_number="Adafruit #3660"]
  R3 = Resistor [tolerance=±5% power=0.25 resistance=220 package=THT]
  JP2 = Header 8 [package=1x08_smd_alt]
  U5 = LoRaWAN RN2483/RN2903 Breakout board

nets:
  3V3: R1.pin_0, U4.3V3, OLED2.VDD, DHT1.VDD, GY2.pin7, JP2.6
  N1: R1.pin_1, U4.A0, R3.Pin_0
  SCL: U4.D1, OLED2.SCK, Part2.SCL, GY2.pin3, Part4.SCK/SCL
  SDA: U4.D2, OLED2.SDA, Part2.SDA, GY2.pin4, Part4.SDI/SDA
  N2: U4.D4, DHT1.DATA
  GND: U4.GND, OLED2.GND, Part2.GND, Part3.GND, DHT1.GND, GY2.pin2, Part4.GND, R3.Pin_1, JP2.8
  SCK: U4.D5, Part3.SCK
  MISO: U4.D6, Part3.MISO_3.3V
  MOSI: U4.D7, Part3.MOSI
  SS: U4.D8, Part3.SS
  RX: U4.RX, JP2.1
  TX: U4.TX, JP2.2
  Vin: U4.Vin, Part2.5V, Part3.VIN, Part4.VCC
  N3: U5.1, U5.2, U5.5, U5.6, U5.7, U5.11, U5.12, U5.13

notes:
  Group 3 - Transporter

custom parts:
  NodeMCU V1.0: ESP8266 based NodeMCU
  OLED 128x64 I2C Monochrome Display GND-VDD: OLED 128x64 I2C Monochrome Display. Note: there are two variants of this part, this one is the GND VDD SCK SDA variant. The other is VDD GND SCK SDA. Make sure you select the part that matches your module as using the incorrect part will probably destroy your module! In addition the mounting holes are marked on silkscreen but not by default drilled. If you want drilled mounting holes, copy a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
  Adafruit SPI Flash SD Card: This breakout is for a fascinating chip - it looks like an SPI Flash storage chip (like the GD25Q16) but its really an SD card, in an SMT chip format. What that means is that you wire up like an SD card breakout, and use the SD card libraries you already have for your microcontroller. For example, you can use the built in SD library in Arduino, or for CircuitPython we have an sdcard library.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
  DHT11 Humitidy and Temperature Sensor: DHT11 Humidity and Temperature Sensor
  MPU-6050 Board GY-521: Acelerometro y Giroscopio MPU-6050 Board GY-521
  LoRaWAN RN2483/RN2903 Breakout board: This breakout board offers an affordable solution for makers working with the popular RN2483A and RN2903A LoRa transceivers from Microchip, widely used for LoRaWAN (Commonly called just RN2483 and RN2903, or collectively, RN2xx3). The layout of this breakout board is based on the the datasheet reference designs. This board breaks out all 14 GPIO pins to a row of 0.1" pin header, and the power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
