# Fritzing sketch Group3_final (saved by Fritzing 0.9.9b)
circuit board: 13.8693cm x 10.5484cm
breadboards: 1

parts:
  U6 = NodeMCU V1.0
  PhotoResistor = Photocell (LDR) [package=THT]
  MPU = MPU-6050 Board GY-521 [form="♀ (female)" package=THT]
  RTC = ZS-042 RTC Module
  BME680 = Adafruit BME680 [part_number="Adafruit #3660"]
  LoRa_RN2483_-_Not_Connected_Due_to_Symbol_Error = LoRaWAN RN2483/RN2903 Breakout board  # not connected
  PowerJack = Power Jack [package=power_jack_pth_lock]
  R5 = Resistor [tolerance=±5% power=0.25 resistance=220 package=THT]
  microSD2 = MicroSD Card Module
  Jumper_Replacement_Lora = Header 8 [package=1x08_smd]
  OLED1 = OLED 128x64 I2C Monochrome Display

nets:
  RX mcu: U6.D1, Jumper_Replacement_Lora.2
  TX mcu: U6.D2, Jumper_Replacement_Lora.1
  SDA: U6.D3, MPU.pin4, RTC.SDA, BME680.SDA, OLED1.SDA
  SCL: U6.D4, MPU.pin3, RTC.SCL, BME680.SCL, OLED1.SCK
  VCC: U6.3V3, PhotoResistor.pin_0, MPU.pin7, RTC.VCC, BME680.VCC, microSD2.VCC, Jumper_Replacement_Lora.6, OLED1.VDD
  GND: U6.GND, MPU.pin2, RTC.GND, BME680.GND, PowerJack.GND, R5.Pin_1, microSD2.GND, Jumper_Replacement_Lora.8, OLED1.GND
  CLK: U6.D5, microSD2.SCK
  MISO: U6.D6, microSD2.MISO
  MOSI: U6.D7, microSD2.MOSI
  CS: U6.D8, microSD2.SS
  VIN: U6.Vin, PowerJack.PWR
  RST: U6.RST, Jumper_Replacement_Lora.5
  N1: U6.A0, PhotoResistor.pin_1, R5.Pin_0

notes:
  Group 3 - Transport

custom parts:
  NodeMCU V1.0: ESP8266 based NodeMCU
  MPU-6050 Board GY-521: Acelerometro y Giroscopio MPU-6050 Board GY-521
  LoRaWAN RN2483/RN2903 Breakout board: This breakout board offers an affordable solution for makers working with the popular RN2483A and RN2903A LoRa transceivers from Microchip, widely used for LoRaWAN (Commonly called just RN2483 and RN2903, or collectively, RN2xx3). The layout of this breakout board is based on the the datasheet reference designs. This board breaks out all 14 GPIO pins to a row of 0.1" pin header, and the power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
  MicroSD Card Module: A common microSD card module.
