# Fritzing sketch Group3 (saved by Fritzing 0.9.3b)
breadboards: 1

parts:
  U1 = ESP32S-HiLetgo [part_number=ESP32S-HiLetgo]
  MH-Real-Time_Clock_Module_2 = RTC_DS1302_module
  Part1 = Adafruit SPI Flash SD Card [part_number="Adafruit #4899"]
  GY1 = MPU-6050 Board GY-521 [form="♀ (female)" package=THT]
  OLED1 = OLED 128x64 I2C Monochrome Display GND-VDD
  R1 = Photocell (LDR) [package=THT]  # not connected
  S2 = D2F-FL Omron Snap Action Limit Switch with Level  # not connected
  M1 = BME680
  U2 = LoRaWAN RN2483/RN2903 Breakout board

nets:
  3.3V: U1.3.3, Part1.3.3V, GY1.pin1, M1.Pin_6, M1.Pin_17, U2.3V3
  GND: U1.GND, MH-Real-Time_Clock_Module_2.GND, Part1.GND, GY1.pin2, OLED1.GND, M1.Pin_5, M1.Pin_18, U2.GND
  VIN: U1.VIN, MH-Real-Time_Clock_Module_2.VCC, OLED1.VDD
  N1: U1.GPIO16, U2.TX
  N2: U1.GPIO17, U2.RX
  N3: U1.GPIO18, Part1.SCK
  N4: U1.GPIO19, Part1.MISO_3.3V
  N5: U1.GPIO21, GY1.pin4, OLED1.SDA
  N6: U1.GPIO22, GY1.pin3, OLED1.SCK
  N7: U1.GPIO23, Part1.MOSI

custom parts:
  ESP32S-HiLetgo: HiLetgo ESP-WROOM-32 ESP32 ESP-32S Development Board 2.4GHz Dual-Mode WiFi + Bluetooth Dual Cores Microcontroller The ESP32 integrated with Antenna switches, RF Balun, power amplifiers, low-noise amplifiers, filters, and management modules, and the entire solution occupies the least area of PCB. 2.4 GHz Wi-Fi plus Bluetooth dual-mode chip, with TSMC Ultra-low power consumption 40nm technology,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
  RTC_DS1302_module: Arduino module DS1302 SPI Real Time Clock
  Adafruit SPI Flash SD Card: This breakout is for a fascinating chip - it looks like an SPI Flash storage chip (like the GD25Q16) but its really an SD card, in an SMT chip format. What that means is that you wire up like an SD card breakout, and use the SD card libraries you already have for your microcontroller. For example, you can use the built in SD library in Arduino, or for CircuitPython we have an sdcard library.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
  MPU-6050 Board GY-521: Acelerometro y Giroscopio MPU-6050 Board GY-521
  OLED 128x64 I2C Monochrome Display GND-VDD: OLED 128x64 I2C Monochrome Display. Note: there are two variants of this part, this one is the GND VDD SCK SDA variant. The other is VDD GND SCK SDA. Make sure you select the part that matches your module as using the incorrect part will probably destroy your module! In addition the mounting holes are marked on silkscreen but not by default drilled. If you want drilled mounting holes, copy a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
  D2F-FL Omron Snap Action Limit Switch with Level: Snap action switch with stainless steel lever.
  BME680: The SparkFun BME680 Environmental Sensor is a breakout that combines a gas sensor with temperature, humidity and barometric pressure sensing for a complete environmental sensor in a single package. The gas sensor on the BME680 can detect a wide variety of volatile organic compounds (or VOC for short) to monitor indoor air quality. Combine that with precise temperature, humidity, and barometric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
  LoRaWAN RN2483/RN2903 Breakout board: This breakout board offers an affordable solution for makers working with the popular RN2483A and RN2903A LoRa transceivers from Microchip, widely used for LoRaWAN (Commonly called just RN2483 and RN2903, or collectively, RN2xx3). The layout of this breakout board is based on the the datasheet reference designs. This board breaks out all 14 GPIO pins to a row of 0.1" pin header, and the power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
